// Digital circuit main.dig as structural Verilog
module main (
  input  clk,
  input  reset,
  input  [7:0] kb_data,
  input  [12:0] disp_read,
  input  kb_en,
  output [39:0] WB_MUX,
  output [31:0] DISP,
  output [11:0] iropcode,
  output [23:0] pc_out
);

  wire ctrl_bank_en, ctrl_branch_en, ctrl_cycles, ctrl_enc, ctrl_flags_we, ctrl_ir_sel, ctrl_jump_type,
       ctrl_mem_rd, ctrl_mem_wr, ctrl_mul_div_en, ctrl_pc_cond, ctrl_pc_link_WE, ctrl_pc_src, ctrl_reg_we,
       ctrl_shift_op, ctrl_wb_sel, HALT_IN, IR_ADDR, mem_rd_out, mn_enc, nflag_A_zero, p_enc, pc_link,
       pc_save, seq_exec, seq_fetch;
  wire [1:0] ctrl_sp_out;
  wire [2:0] ctrl_bus_sel, ctrl_csel;
  wire [3:0] BANK_SEL, ctrl_byte_sel;
  wire [5:0] ir_addr_a, ir_addr_b, ir_addr_c, ir_addr_w;
  wire [7:0] csr_flags, ctrl_lut_A, ctrl_lut_B;
  wire [23:0] mem_addr, sp_out;
  wire [39:0] alu_out, ir_bus, mem_din, mem_ram_out, reg_a, reg_b, reg_c;

  // alu_control alu_control_1: pin names not known; wires that end beside it: iropcode, ctrl_lut_A, ctrl_csel, ctrl_flags_we, ctrl_lut_B, ctrl_shift_op, ctrl_mul_div_en, ctrl_enc
  // ir_reg_control ir_reg_control_1: pin names not known; wires that end beside it: iropcode, ctrl_ir_sel, ctrl_wb_sel, ctrl_reg_we
  mem_bus_control mem_bus_control_1 (.op(iropcode), .ctrl_bussel(ctrl_bus_sel));
  // mem_io_control mem_io_control_1: pin names not known; wires that end beside it: iropcode, seq_fetch, ctrl_bank_en, ctrl_mem_rd, ctrl_mem_wr, ctrl_byte_sel
  // pc_control pc_control_1: pin names not known; wires that end beside it: seq_exec, iropcode, ctrl_branch_en, ctrl_jump_type, ctrl_pc_src, ctrl_pc_link_WE, ctrl_cycles, ctrl_pc_cond, ctrl_sp_out, HALT_IN
  alu_40b_final alu_40b_final_1 (
    .lutA(ctrl_lut_A), .lutB(ctrl_lut_B), .A(reg_a), .B(ir_bus), .C(reg_c), .csel(ctrl_csel),
    .FLAG_WE(ctrl_flags_we), .CLK(clk), .OUT(alu_out), .csr(csr_flags));
  register register_1 (
    .WE(ctrl_reg_we), .DATA_W(WB_MUX), .ADDR_A(ir_addr_a), .ADDR_B(ir_addr_b), .ADDR_W(ir_addr_w),
    .EXEC(seq_exec), .clk(clk), .BANK_SEL(BANK_SEL), .Bank_en(ctrl_bank_en), .ADDR_C(ir_addr_c),
    .DATA_A(reg_a), .DATA_B(reg_b), .DATA_C(reg_c));
  // mul_div mul_div_1: pin names not known; wires that end beside it: ir_bus, ctrl_shift_op, ctrl_mul_div_en, reg_a, ctrl_enc, p_enc, nflag_A_zero, mn_enc
  vga vga_1 (
    .mem_addr(mem_addr), .disp_rd_addr(disp_read), .clk(clk), .mem_wr(ctrl_mem_wr), .mem_din(WB_MUX),
    .dout(DISP));
  // ir ir_1: pin names not known; wires that end beside it: mem_din, seq_fetch, clk, ctrl_ir_sel, reg_b, iropcode, ir_addr_a, ir_addr_b, ir_addr_w, IR_ADDR, ir_bus, BANK_SEL, ir_addr_c
  byte_lane_decoder byte_lane_decoder_1 (
    .mem_in(mem_ram_out), .sel_in(ctrl_byte_sel), .io_data_in(kb_data), .mem_out(mem_din));
  RAMDualPort #(.AddrBits(24), .Bits(40)) ramdualport_1 (
    .A(mem_addr), .Din(WB_MUX), .str(ctrl_mem_wr), .C(clk), .ld(mem_rd_out), .D(mem_ram_out));
  // program_counter program_counter_1: pin names not known; wires that end beside it: mem_din, alu_out, ctrl_pc_src, IR_ADDR, reset, ctrl_cycles, csr_flags, ctrl_pc_cond, ctrl_jump_type, ctrl_branch_en, 1'b1, HALT_IN, kb_en, 1'b1, 1'b1, 1'b1, ctrl_pc_link_WE, clk, pc_out, pc_save, seq_fetch, seq_exec, pc_link
  sp sp_1 (.sp_op(ctrl_sp_out), .CLK(clk), .Reset(reset), .sp_load_in(alu_out), .seq_exec(seq_exec), .sp_out(sp_out));
  // wb_mux wb_mux_1: pin names not known; wires that end beside it: ctrl_wb_sel, alu_out, p_enc, pc_save, mem_din, reg_a, ir_bus, csr_flags, mn_enc, WB_MUX
  // bus_arbitration bus_arbitration_1: pin names not known; wires that end beside it: seq_fetch, IR_ADDR, ctrl_mem_rd, ctrl_bus_sel, reg_b, pc_out, sp_out, alu_out, mem_addr, mem_rd_out

  // Other names for the same wires on the sheet: disp_out[31:0] = DISP; disp_read_addr[12:0] = disp_read;
  //   ir_opcode[11:0] = iropcode; wb_data[39:0] = WB_MUX

  // Notes on the sheet:
  //   Control Unit
  //   ALU
  //   Shift - Encoder
  //   Memory
  //   Instruction Register
  //   Program Counter
  //   Data Bus Switch
endmodule
